# Fritzing sketch project_circuit (saved by Fritzing 0.9.3b)
breadboards: 2

parts:
  Mod1 = PicoW
  U1 = Voltage Regulator - Variable [package="TO220 [THT]"]
  C1 = Capacitor [package=cap-pth-small]
  R1 = Resistor [tolerance=±5% resistance=220 package="0402 [SMD]"]
  R3 = Rotary Potentiometer (Large) [maximum_resistance=100kΩ package=THT]
  C2 = Capacitor Polarized [package=panasonic_c]
  M1 = DC Motor [part_number="DC Pump"]
  OMRON1 = OMRON PCB Power Relay – G5LE [part_number=Relay package=THT]
  Part1 = Solar Panel [package="Renogy 50 Watts 12 Volt Monocrystalline Bendable Solar Panel"]
  Part2 = Solar Charge Controller [part_number="HGX Series Solar Charge Controller PWM" package=PWM-Model]
  BAT1 = 12 battery [package=battery]
  U2 = SWITCH-SPST-2 [package=switch-spst-vertical]
  M2 = sim800L v2 evb
  OLED1 = OLED 128x64 I2C Monochrome Display GND-VDD

nets (from the breadboard view):
  N1: Mod1.connector0, OMRON1.C
  N2: Mod1.connector3, OLED1.SDA
  N3: Mod1.connector4, OLED1.SCK
  N4: Mod1.connector9, M2.pin_4
  N5: Mod1.connector10, M2.pin_3
  N6: Mod1.connector37, M2.pin_2, M2.pin_6, OLED1.GND
  N7: Mod1.connector38, U1.OUT, R1.Pin_1, C2.+, M2.pin_7, OLED1.VDD
  N8: U1.ADJ, R3.leg1
  N9: U1.IN, C1.1, OMRON1.COIL2, U2.P
  N10: C1.2, R3.leg2, C2.-, M1.pin_2, OMRON1.COIL1, Part2.Connector_6
  N11: R1.Pin_0, R3.wiper
  N12: M1.pin_1, OMRON1.B
  N13: Part1.Connector_1, Part2.Connector_1
  N14: Part1.Connector_2, Part2.Connector_2
  N15: Part2.Connector_3, BAT1.+
  N16: Part2.Connector_4, BAT1.-
  N17: Part2.Connector_5, U2.O

custom parts:
  Solar Panel: Renogy 50 Watts 12 Volt Solar Panel
  Solar Charge Controller: PWM-Solar Charge Controller
  12 battery: 12V lead acid type battery, like the Husqvarna YTH2448 12V 35AH battery. This is the mini version 1/4 the size of the actual battery to be closer to typical breadboard parts (around 2in wide rathher than 7in). The pads in pcb are sized to accomidate up to 14ga wire (as these batterys will deliver high currents.)
  sim800L v2 evb: sim800L v2 evb GSM module.
  OLED 128x64 I2C Monochrome Display GND-VDD: OLED 128x64 I2C Monochrome Display. Note: there are two variants of this part, this one is the GND VDD SCK SDA variant. The other is VDD GND SCK SDA. Make sure you select the part that matches your module as using the incorrect part will probably destroy your module! In addition the mounting holes are marked on silkscreen but not by default drilled. If you want drilled mounting holes, copy a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
